# Fritzing sketch depth-repeater-board (saved by Fritzing 0.9.3b)
stripboards: 1

parts:
  U1 = MAX485 [package=dil08]
  J1 = Camdenboss CTB0158-2 [part_number=CTB0158-2 package=THT]
  J2 = Camdenboss CTB0158-2 [part_number=CTB0158-2 package=THT]
  IC1 = Voltage Regulator [package=78xxl]
  J3 = Camdenboss CTB0158-2 [part_number=CTB0158-2 package=THT]
  Nano1 = Arduino Nano v2.3
  J4 = Camdenboss CTB0158-2 [part_number=CTB0158-2 package=THT]

nets:
  N1: U1.RO, Nano1.D0RX
  N2: U1.RE, Nano1.D2
  GND: U1.GND, IC1.GND, J3.pin1, Nano1.GND, J4.pin1
  N3: U1.A, J2.pin1
  N4: U1.B, J2.pin2
  VCC: U1.VCC, IC1.OUT, Nano1.+5V
  N5: J1.pin1, Nano1.D12
  N6: J1.pin2, Nano1.D3
  N7: IC1.IN, J3.pin2, J4.pin2
